# Fritzing sketch BSetUpRed (saved by Fritzing 0.9.9b)
breadboards: 1

parts:
  J4 = female pin header, 2 pins [form="♀ (female)"]
  J5 = female pin header, 2 pins [form="♀ (female)"]
  J6 = female pin header, 2 pins [form="♀ (female)"]
  J7 = female pin header, 2 pins [form="♀ (female)"]
  J8 = female pin header, 2 pins [form="♀ (female)"]
  J9 = female pin header, 2 pins [form="♀ (female)"]
  J10 = female pin header, 2 pins [form="♀ (female)"]
  J11 = female pin header, 2 pins [form="♀ (female)"]
  J12 = shrouded pin header, 8 pins [form="♂ (shrouded male)"]
  J13 = Power Jack [package=power_jack_pth_lock]
  J14 = Power Jack [package=power_jack_slot]
  J15 = Power Jack [package=power_jack_slot]
  J16 = Power Jack [package=power_jack_slot]
  J18 = Camdenboss CTB0158-8 [part_number=CTB0158-8 package=THT]  # not connected
  J19 = Camdenboss CTB0158-8 [part_number=CTB0158-8 package=THT]
  J20 = Camdenboss CTB0158-10 [part_number=CTB0158-10 package=THT]

nets:
  GND: J4.pin1, J4.pin2, J5.pin1, J5.pin2, J6.pin1, J6.pin2, J7.pin1, J7.pin2, J8.pin2, J12.pin4, J13.GND, J15.GND, J19.terminal_2, J19.terminal_4, J19.terminal_6, J19.terminal_8
  N1: J8.pin1, J12.pin3, J13.GNDBREAK
  N2: J9.pin1, J12.pin1, J20.terminal_2
  N3: J9.pin2, J12.pin2, J14.GND, J19.terminal_3, J19.terminal_7
  N4: J10.pin1, J12.pin6, J19.terminal_1, J19.terminal_5
  N5: J10.pin2, J12.pin5, J16.GNDBREAK
  N6: J11.pin1, J12.pin8, J15.GNDBREAK
  N7: J11.pin2, J12.pin7, J20.terminal_3

notes:
  1             2             3             4              5             6             7             8
  +      -
  +5V
  A
  B
  Z
  GND
  18
  19
  Bpod Rotary Encoder Module
  Bpod Analog Input Module
  Input Channels
  15-pin breadboard
